# Fritzing sketch spongebot circuit (saved by Fritzing 0.9.3b)
breadboards: 1

parts:
  Part1 = Arduino Uno (Rev3)
  BT1 = Bluetooth HC-06d [package=THT]
  S1 = H-Bridge with L298N
  VCC1 = Battery
  Mod1 = KY-008 Laser Transmitter Module [package="Breakout board"]
  Mod2 = KY-008 Laser Transmitter Module [package="Breakout board"]
  M1 = Getriebemotor
  M2 = Getriebemotor
  SERVO1 = Tower Pro SG90 servo [part_number=101246]
  SERVO2 = Tower Pro SG90 servo [part_number=101246]

nets:
  N1: Part1.D8, SERVO1.Signal
  N2: Part1.D9_PWM, S1.IN4
  N3: Part1.D10_PWM/SS, S1.IN3
  N4: Part1.D12/MISO, Mod1.S
  N5: Part1.D13/SCK, Mod2.S
  GND: Part1.GND, BT1.GND, S1.GND, VCC1.-, Mod1.-, Mod2.-, SERVO1.GND, SERVO2.GND
  N6: Part1.D0/RX, BT1.TXD
  N7: Part1.D1/TX, BT1.RXD
  N8: Part1.D3_PWM, S1.IN1
  N9: Part1.D4, S1.IN2
  N10: Part1.D7, SERVO2.Signal
  +5V: BT1.VCC, S1.5V, Mod1.NC, Mod2.NC, SERVO1.+5V, SERVO2.+5V
  N11: S1.12V, VCC1.+
  N12: S1.ENA, S1.ENA-5V
  N13: S1.ENB, S1.ENB-5V
  N14: S1.M1-01, M2.pin_2
  N15: S1.M1-02, M2.pin_1
  N16: S1.M2-01, M1.pin_2
  N17: S1.M2-02, M1.pin_1

custom parts:
  Bluetooth HC-06d: Bluetooth HC-06 - face down, pins down 16.5mm x 37.5mm PCB
  H-Bridge with L298N: h-bridge
  Battery: Your standard 2x 18650 battery pack (14.7 Volts)
  KY-008 Laser Transmitter Module: KY-008 Laser Transmitter Module, emits a dot shaped red laser beam.
  Tower Pro SG90 servo: Original file by John De Cristofaro http://www.adafruit.com/products/1449 Adafruit Feedback Servo (Small) Edited by: e-radionica.com 28/9/2015
